# Fritzing sketch udkKontroll (saved by Fritzing 0.7.10b)
breadboards: 1

parts:
  AtTiny2313-20PU1 = IC, DIP package, 20 pins [chip_label=AtTiny2313-20PU spacing=300mil]
  C1 = Ceramic Disk Capacitor [package=THT]
  XTAL1 = Crystal [package=THT]
  C2 = Ceramic Disk Capacitor [package=THT]
  D1 = Zener Diode [part_number=1N4732A breakdown_voltage=3.6V package="Melf DO-213 AB [SMD]"]
  D2 = Zener Diode [part_number=1N4732A breakdown_voltage=3.6V package="Melf DO-213 AB [SMD]"]
  USB1 = USB connector [package=THT]
  R1 = 2.2k Ω Resistor [package=THT]
  R2 = 68 Ω Resistor [package=THT]
  R3 = 68 Ω Resistor [package=THT]
  C3 = Electrolytic Capacitor [package=THT]
  C4 = Ceramic Capacitor [capacitance=100nF package="100 mil [THT, multilayer]"]
  J1 = female pin header, 8 pins [form="♀ (female)"]
  J2 = female pin header, 5 pins [form="♀ (female)"]

nets:
  N1: AtTiny2313-20PU1.pin2, J2.pin5
  N2: AtTiny2313-20PU1.pin3, J2.pin4
  N3: AtTiny2313-20PU1.pin4, C1.pin_1, XTAL1.pin_0
  N4: AtTiny2313-20PU1.pin5, XTAL1.pin_1, C2.pin_1
  N5: AtTiny2313-20PU1.pin6, R2.Pin_0
  N6: AtTiny2313-20PU1.pin7, R3.Pin_0
  N7: AtTiny2313-20PU1.pin8, J2.pin3
  N8: AtTiny2313-20PU1.pin9, J2.pin2
  GND: AtTiny2313-20PU1.pin10, C1.pin_0, C2.pin_0, D1.anode, D2.anode, USB1.GND, USB1.chassis5, USB1.chassis6, C3.-, C4.0
  N9: AtTiny2313-20PU1.pin11, J2.pin1
  N10: AtTiny2313-20PU1.pin12, J1.pin8
  N11: AtTiny2313-20PU1.pin13, J1.pin7
  N12: AtTiny2313-20PU1.pin14, J1.pin6
  N13: AtTiny2313-20PU1.pin15, J1.pin5
  N14: AtTiny2313-20PU1.pin16, J1.pin4
  N15: AtTiny2313-20PU1.pin17, J1.pin3
  N16: AtTiny2313-20PU1.pin18, J1.pin2
  N17: AtTiny2313-20PU1.pin19, J1.pin1
  5V: AtTiny2313-20PU1.pin20, USB1.5V, R1.Pin_0, C3.+, C4.1
  N18: D1.cathode, USB1.d+, R2.Pin_1
  N19: D2.cathode, USB1.d-, R1.Pin_1, R3.Pin_1

custom parts:
  Ceramic Disk Capacitor: A 22 pF Ceramic Disk Capacitor
